// Digital circuit day23.dig as structural Verilog
module day23 (
  input  C
);

  wire comparator_1_eq, day23_parser_1_out_en, node0_out_en, node1_out_en, node2_out_en, node3_out_en,
       node4_out_en, node5_out_en, node6_out_en, node7_out_en, node8_out_en, node9_out_en, node10_out_en,
       node11_out_en, node12_out_en, node13_out_en, node14_out_en, node16_out_en, node17_out_en,
       node18_out_en, node19_out_en, node20_out_en, node21_out_en, node22_out_en, node23_out_en,
       node24_out_en, node25_out_en, node26_out_en, node27_out_en, node28_out_en, node29_out_en,
       node30_out_en, node32_out_en, node33_out_en, node34_out_en, node35_out_en, node36_out_en,
       node37_out_en, node38_out_en, node39_out_en, node40_out_en, node41_out_en, node42_out_en,
       node43_out_en, node44_out_en, node45_out_en, node46_out_en, node48_out_en, out15_en, out31_en,
       out47_en, out255_en, shifter_1_p4, shifter_1_p5, shifter_1_p6, shifter_1_p7, shifter_1_p8,
       shifter_1_p9, shifter_1_p10, shifter_2_p2, shifter_2_p4, shifter_2_p5, shifter_2_p6, shifter_2_p7,
       shifter_2_p8, shifter_2_p9, shifter_2_p10, shifter_3_p2, shifter_3_p4, shifter_3_p5, shifter_3_p6,
       shifter_3_p7, shifter_3_p8, shifter_3_p9, shifter_3_p10, shifter_4_p2, shifter_4_p4, shifter_4_p5,
       shifter_4_p6, shifter_4_p7, shifter_4_p8, shifter_4_p9, shifter_4_p10, shifter_5_p2, shifter_5_p4,
       shifter_5_p5, shifter_5_p6, shifter_5_p7, shifter_5_p8, shifter_5_p9, shifter_5_p10, shifter_6_p2,
       shifter_6_p4, shifter_6_p5, shifter_6_p6, shifter_6_p7, shifter_6_p8, shifter_6_p9, shifter_6_p10,
       shifter_6_p11, undriven, undriven_3, undriven_5, undriven_7, undriven_8;
  wire [15:0] counter_1_out;
  wire [31:0] node0_out_cnt, node1_out_cnt, node2_out_cnt, node3_out_cnt, node4_out_cnt, node5_out_cnt,
       node6_out_cnt, node7_out_cnt, node8_out_cnt, node9_out_cnt, node10_out_cnt, node11_out_cnt,
       node12_out_cnt, node13_out_cnt, node14_out_cnt, node15_out_cnt, node16_out_cnt, node17_out_cnt,
       node18_out_cnt, node19_out_cnt, node20_out_cnt, node21_out_cnt, node22_out_cnt, node23_out_cnt,
       node24_out_cnt, node25_out_cnt, node26_out_cnt, node27_out_cnt, node28_out_cnt, node29_out_cnt,
       node30_out_cnt, node31_out_cnt, node32_out_cnt, node33_out_cnt, node34_out_cnt, node35_out_cnt,
       node36_out_cnt, node37_out_cnt, node38_out_cnt, node39_out_cnt, node40_out_cnt, node41_out_cnt,
       node42_out_cnt, node43_out_cnt, node44_out_cnt, node45_out_cnt, node46_out_cnt, node47_out_cnt,
       node48_out_cnt, node49_out_cnt;
  wire [63:0] day23_parser_1_out_val, node1_out_val, node2_out_val, node3_out_val, node4_out_val,
       node5_out_val, node6_out_val, node7_out_val, node8_out_val, node9_out_val, node10_out_val,
       node11_out_val, node12_out_val, node13_out_val, node14_out_val, node17_out_val, node18_out_val,
       node19_out_val, node20_out_val, node21_out_val, node22_out_val, node23_out_val, node24_out_val,
       node25_out_val, node26_out_val, node27_out_val, node28_out_val, node29_out_val, node30_out_val,
       node33_out_val, node34_out_val, node35_out_val, node36_out_val, node37_out_val, node38_out_val,
       node39_out_val, node40_out_val, node41_out_val, node42_out_val, node43_out_val, node44_out_val,
       node45_out_val, node46_out_val, node49_out_val, out15_val, out31_val, out47_val, out255_val,
       undriven_2, undriven_4, undriven_6, undriven_9;

  day23_node #(.generic("label := \"node0\";")) node0 (
    .C(C), .out_en(node0_out_en), .in_en(out255_en), .out_cnt(node0_out_cnt));  // open: addr_next, out_val, addr, in_val
  day23_node #(.generic("label := \"node1\";")) node1 (
    .C(C), .out_en(node1_out_en), .out_val(node1_out_val), .in_en(undriven), .in_val(undriven_2),
    .out_cnt(node1_out_cnt));  // open: addr_next, out_busy, addr, in_busy
  day23_node #(.generic("label := \"node2\";")) node2 (
    .C(C), .out_en(node2_out_en), .out_val(node2_out_val), .in_en(node1_out_en), .in_val(node1_out_val),
    .out_cnt(node2_out_cnt));  // open: addr_next, out_busy, addr, in_busy
  day23_node #(.generic("label := \"node3\";")) node3 (
    .C(C), .out_en(node3_out_en), .out_val(node3_out_val), .in_en(node2_out_en), .in_val(node2_out_val),
    .out_cnt(node3_out_cnt));  // open: addr_next, out_busy, addr, in_busy
  day23_node #(.generic("label := \"node4\";")) node4 (
    .C(C), .out_en(node4_out_en), .out_val(node4_out_val), .in_en(node3_out_en), .in_val(node3_out_val),
    .out_cnt(node4_out_cnt));  // open: addr_next, out_busy, addr, in_busy
  day23_node #(.generic("label := \"node5\";")) node5 (
    .C(C), .out_en(node5_out_en), .out_val(node5_out_val), .in_en(node4_out_en), .in_val(node4_out_val),
    .out_cnt(node5_out_cnt));  // open: addr_next, out_busy, addr, in_busy
  day23_node #(.generic("label := \"node6\";")) node6 (
    .C(C), .out_en(node6_out_en), .out_val(node6_out_val), .in_en(node5_out_en), .in_val(node5_out_val),
    .out_cnt(node6_out_cnt));  // open: addr_next, out_busy, addr, in_busy
  day23_node #(.generic("label := \"node7\";")) node7 (
    .C(C), .out_en(node7_out_en), .out_val(node7_out_val), .in_en(node6_out_en), .in_val(node6_out_val),
    .out_cnt(node7_out_cnt));  // open: addr_next, out_busy, addr, in_busy
  day23_node #(.generic("label := \"node8\";")) node8 (
    .C(C), .out_en(node8_out_en), .out_val(node8_out_val), .in_en(node7_out_en), .in_val(node7_out_val),
    .out_cnt(node8_out_cnt));  // open: addr_next, out_busy, addr, in_busy
  day23_node #(.generic("label := \"node9\";")) node9 (
    .C(C), .out_en(node9_out_en), .out_val(node9_out_val), .in_en(node8_out_en), .in_val(node8_out_val),
    .out_cnt(node9_out_cnt));  // open: addr_next, out_busy, addr, in_busy
  day23_node #(.generic("label := \"node10\";")) node10 (
    .C(C), .out_en(node10_out_en), .out_val(node10_out_val), .in_en(node9_out_en), .in_val(node9_out_val),
    .out_cnt(node10_out_cnt));  // open: addr_next, out_busy, addr, in_busy
  day23_node #(.generic("label := \"node11\";")) node11 (
    .C(C), .out_en(node11_out_en), .out_val(node11_out_val), .in_en(node10_out_en), .in_val(node10_out_val),
    .out_cnt(node11_out_cnt));  // open: addr_next, out_busy, addr, in_busy
  day23_node #(.generic("label := \"node12\";")) node12 (
    .C(C), .out_en(node12_out_en), .out_val(node12_out_val), .in_en(node11_out_en), .in_val(node11_out_val),
    .out_cnt(node12_out_cnt));  // open: addr_next, out_busy, addr, in_busy
  day23_node #(.generic("label := \"node13\";")) node13 (
    .C(C), .out_en(node13_out_en), .out_val(node13_out_val), .in_en(node12_out_en), .in_val(node12_out_val),
    .out_cnt(node13_out_cnt));  // open: addr_next, out_busy, addr, in_busy
  day23_node #(.generic("label := \"node14\";")) node14 (
    .C(C), .out_en(node14_out_en), .out_val(node14_out_val), .in_en(node13_out_en), .in_val(node13_out_val),
    .out_cnt(node14_out_cnt));  // open: addr_next, out_busy, addr, in_busy
  day23_node #(.generic("label := \"node15\";")) node15 (
    .C(C), .out_val(out15_val), .in_en(node14_out_en), .in_val(node14_out_val), .out_cnt(node15_out_cnt));  // open: addr_next, out_en, out_busy, addr, in_busy
  // Probe on node0_out_cnt
  // Probe on node1_out_cnt
  // Probe on node2_out_cnt
  // Probe on node3_out_cnt
  // Probe on node4_out_cnt
  // Probe on node5_out_cnt
  // Probe on node6_out_cnt
  // Probe on node7_out_cnt
  // Probe on node8_out_cnt
  // Probe on node9_out_cnt
  // Probe on node10_out_cnt
  // Probe on node11_out_cnt
  // Probe on node12_out_cnt
  // Probe on node13_out_cnt
  // Probe on node14_out_cnt
  // Probe on node15_out_cnt
  day23_node #(.generic("label := \"node16\";")) node16 (
    .C(C), .out_en(node16_out_en), .in_en(out15_en), .out_cnt(node16_out_cnt));  // open: addr_next, out_val, addr, in_val
  day23_node #(.generic("label := \"node17\";")) node17 (
    .C(C), .out_en(node17_out_en), .out_val(node17_out_val), .in_en(undriven_3), .in_val(undriven_4),
    .out_cnt(node17_out_cnt));  // open: addr_next, out_busy, addr, in_busy
  day23_node #(.generic("label := \"node18\";")) node18 (
    .C(C), .out_en(node18_out_en), .out_val(node18_out_val), .in_en(node17_out_en), .in_val(node17_out_val),
    .out_cnt(node18_out_cnt));  // open: addr_next, out_busy, addr, in_busy
  day23_node #(.generic("label := \"node19\";")) node19 (
    .C(C), .out_en(node19_out_en), .out_val(node19_out_val), .in_en(node18_out_en), .in_val(node18_out_val),
    .out_cnt(node19_out_cnt));  // open: addr_next, out_busy, addr, in_busy
  day23_node #(.generic("label := \"node20\";")) node20 (
    .C(C), .out_en(node20_out_en), .out_val(node20_out_val), .in_en(node19_out_en), .in_val(node19_out_val),
    .out_cnt(node20_out_cnt));  // open: addr_next, out_busy, addr, in_busy
  day23_node #(.generic("label := \"node21\";")) node21 (
    .C(C), .out_en(node21_out_en), .out_val(node21_out_val), .in_en(node20_out_en), .in_val(node20_out_val),
    .out_cnt(node21_out_cnt));  // open: addr_next, out_busy, addr, in_busy
  day23_node #(.generic("label := \"node22\";")) node22 (
    .C(C), .out_en(node22_out_en), .out_val(node22_out_val), .in_en(node21_out_en), .in_val(node21_out_val),
    .out_cnt(node22_out_cnt));  // open: addr_next, out_busy, addr, in_busy
  day23_node #(.generic("label := \"node23\";")) node23 (
    .C(C), .out_en(node23_out_en), .out_val(node23_out_val), .in_en(node22_out_en), .in_val(node22_out_val),
    .out_cnt(node23_out_cnt));  // open: addr_next, out_busy, addr, in_busy
  day23_node #(.generic("label := \"node24\";")) node24 (
    .C(C), .out_en(node24_out_en), .out_val(node24_out_val), .in_en(node23_out_en), .in_val(node23_out_val),
    .out_cnt(node24_out_cnt));  // open: addr_next, out_busy, addr, in_busy
  day23_node #(.generic("label := \"node25\";")) node25 (
    .C(C), .out_en(node25_out_en), .out_val(node25_out_val), .in_en(node24_out_en), .in_val(node24_out_val),
    .out_cnt(node25_out_cnt));  // open: addr_next, out_busy, addr, in_busy
  day23_node #(.generic("label := \"node26\";")) node26 (
    .C(C), .out_en(node26_out_en), .out_val(node26_out_val), .in_en(node25_out_en), .in_val(node25_out_val),
    .out_cnt(node26_out_cnt));  // open: addr_next, out_busy, addr, in_busy
  day23_node #(.generic("label := \"node27\";")) node27 (
    .C(C), .out_en(node27_out_en), .out_val(node27_out_val), .in_en(node26_out_en), .in_val(node26_out_val),
    .out_cnt(node27_out_cnt));  // open: addr_next, out_busy, addr, in_busy
  day23_node #(.generic("label := \"node28\";")) node28 (
    .C(C), .out_en(node28_out_en), .out_val(node28_out_val), .in_en(node27_out_en), .in_val(node27_out_val),
    .out_cnt(node28_out_cnt));  // open: addr_next, out_busy, addr, in_busy
  day23_node #(.generic("label := \"node29\";")) node29 (
    .C(C), .out_en(node29_out_en), .out_val(node29_out_val), .in_en(node28_out_en), .in_val(node28_out_val),
    .out_cnt(node29_out_cnt));  // open: addr_next, out_busy, addr, in_busy
  day23_node #(.generic("label := \"node30\";")) node30 (
    .C(C), .out_en(node30_out_en), .out_val(node30_out_val), .in_en(node29_out_en), .in_val(node29_out_val),
    .out_cnt(node30_out_cnt));  // open: addr_next, out_busy, addr, in_busy
  day23_node #(.generic("label := \"node31\";")) node31 (
    .C(C), .out_val(out31_val), .in_en(node30_out_en), .in_val(node30_out_val), .out_cnt(node31_out_cnt));  // open: addr_next, out_en, out_busy, addr, in_busy
  // Probe on node16_out_cnt
  // Probe on node17_out_cnt
  // Probe on node18_out_cnt
  // Probe on node19_out_cnt
  // Probe on node20_out_cnt
  // Probe on node21_out_cnt
  // Probe on node22_out_cnt
  // Probe on node23_out_cnt
  // Probe on node24_out_cnt
  // Probe on node25_out_cnt
  // Probe on node26_out_cnt
  // Probe on node27_out_cnt
  // Probe on node28_out_cnt
  // Probe on node29_out_cnt
  // Probe on node30_out_cnt
  // Probe on node31_out_cnt
  day23_node #(.generic("label := \"node32\";")) node32 (
    .C(C), .out_en(node32_out_en), .in_en(out31_en), .out_cnt(node32_out_cnt));  // open: addr_next, out_val, addr, in_val
  day23_node #(.generic("label := \"node33\";")) node33 (
    .C(C), .out_en(node33_out_en), .out_val(node33_out_val), .in_en(undriven_5), .in_val(undriven_6),
    .out_cnt(node33_out_cnt));  // open: addr_next, out_busy, addr, in_busy
  day23_node #(.generic("label := \"node34\";")) node34 (
    .C(C), .out_en(node34_out_en), .out_val(node34_out_val), .in_en(node33_out_en), .in_val(node33_out_val),
    .out_cnt(node34_out_cnt));  // open: addr_next, out_busy, addr, in_busy
  day23_node #(.generic("label := \"node35\";")) node35 (
    .C(C), .out_en(node35_out_en), .out_val(node35_out_val), .in_en(node34_out_en), .in_val(node34_out_val),
    .out_cnt(node35_out_cnt));  // open: addr_next, out_busy, addr, in_busy
  day23_node #(.generic("label := \"node36\";")) node36 (
    .C(C), .out_en(node36_out_en), .out_val(node36_out_val), .in_en(node35_out_en), .in_val(node35_out_val),
    .out_cnt(node36_out_cnt));  // open: addr_next, out_busy, addr, in_busy
  day23_node #(.generic("label := \"node37\";")) node37 (
    .C(C), .out_en(node37_out_en), .out_val(node37_out_val), .in_en(node36_out_en), .in_val(node36_out_val),
    .out_cnt(node37_out_cnt));  // open: addr_next, out_busy, addr, in_busy
  day23_node #(.generic("label := \"node38\";")) node38 (
    .C(C), .out_en(node38_out_en), .out_val(node38_out_val), .in_en(node37_out_en), .in_val(node37_out_val),
    .out_cnt(node38_out_cnt));  // open: addr_next, out_busy, addr, in_busy
  day23_node #(.generic("label := \"node39\";")) node39 (
    .C(C), .out_en(node39_out_en), .out_val(node39_out_val), .in_en(node38_out_en), .in_val(node38_out_val),
    .out_cnt(node39_out_cnt));  // open: addr_next, out_busy, addr, in_busy
  day23_node #(.generic("label := \"node40\";")) node40 (
    .C(C), .out_en(node40_out_en), .out_val(node40_out_val), .in_en(node39_out_en), .in_val(node39_out_val),
    .out_cnt(node40_out_cnt));  // open: addr_next, out_busy, addr, in_busy
  day23_node #(.generic("label := \"node41\";")) node41 (
    .C(C), .out_en(node41_out_en), .out_val(node41_out_val), .in_en(node40_out_en), .in_val(node40_out_val),
    .out_cnt(node41_out_cnt));  // open: addr_next, out_busy, addr, in_busy
  day23_node #(.generic("label := \"node42\";")) node42 (
    .C(C), .out_en(node42_out_en), .out_val(node42_out_val), .in_en(node41_out_en), .in_val(node41_out_val),
    .out_cnt(node42_out_cnt));  // open: addr_next, out_busy, addr, in_busy
  day23_node #(.generic("label := \"node43\";")) node43 (
    .C(C), .out_en(node43_out_en), .out_val(node43_out_val), .in_en(node42_out_en), .in_val(node42_out_val),
    .out_cnt(node43_out_cnt));  // open: addr_next, out_busy, addr, in_busy
  day23_node #(.generic("label := \"node44\";")) node44 (
    .C(C), .out_en(node44_out_en), .out_val(node44_out_val), .in_en(node43_out_en), .in_val(node43_out_val),
    .out_cnt(node44_out_cnt));  // open: addr_next, out_busy, addr, in_busy
  day23_node #(.generic("label := \"node45\";")) node45 (
    .C(C), .out_en(node45_out_en), .out_val(node45_out_val), .in_en(node44_out_en), .in_val(node44_out_val),
    .out_cnt(node45_out_cnt));  // open: addr_next, out_busy, addr, in_busy
  day23_node #(.generic("label := \"node46\";")) node46 (
    .C(C), .out_en(node46_out_en), .out_val(node46_out_val), .in_en(node45_out_en), .in_val(node45_out_val),
    .out_cnt(node46_out_cnt));  // open: addr_next, out_busy, addr, in_busy
  day23_node #(.generic("label := \"node47\";")) node47 (
    .C(C), .out_val(out47_val), .in_en(node46_out_en), .in_val(node46_out_val), .out_cnt(node47_out_cnt));  // open: addr_next, out_en, out_busy, addr, in_busy
  // Probe on node32_out_cnt
  // Probe on node33_out_cnt
  // Probe on node34_out_cnt
  // Probe on node35_out_cnt
  // Probe on node36_out_cnt
  // Probe on node37_out_cnt
  // Probe on node38_out_cnt
  // Probe on node39_out_cnt
  // Probe on node40_out_cnt
  // Probe on node41_out_cnt
  // Probe on node42_out_cnt
  // Probe on node43_out_cnt
  // Probe on node44_out_cnt
  // Probe on node45_out_cnt
  // Probe on node46_out_cnt
  // Probe on node47_out_cnt
  day23_node #(.generic("label := \"node48\";")) node48 (
    .C(C), .out_en(node48_out_en), .in_en(out47_en), .out_cnt(node48_out_cnt));  // open: addr_next, out_val, addr, in_val
  day23_node #(.generic("label := \"node49\";")) node49 (
    .C(C), .out_val(node49_out_val), .in_en(undriven_7), .in_val(undriven_9), .out_cnt(node49_out_cnt));  // open: addr_next, out_en, out_busy, addr, in_busy
  day23_parser day23_parser_1 (
    .in_en(undriven_8), .in_val(node49_out_val), .address(64'hff), .C(C), .out_en(day23_parser_1_out_en),
    .out_val(day23_parser_1_out_val), .nextout_en(out255_en), .nextout_val(out255_val));
  // Probe on node48_out_cnt
  // Probe on node49_out_cnt
  Counter #(.Bits(16)) counter_1 (.en(day23_parser_1_out_en), .C(C), .clr(1'b0), .out(counter_1_out));  // open: ovf
  // shifter shifter_1: pin names not known; wires that end beside it: day23_parser_1_out_en, day23_parser_1_out_val, C, shifter_1_p4, shifter_1_p5, shifter_1_p6, shifter_1_p7, shifter_1_p8, shifter_1_p9, shifter_1_p10
  // shifter shifter_2: pin names not known; wires that end beside it: day23_parser_1_out_en, shifter_2_p2, C, shifter_2_p4, shifter_2_p5, shifter_2_p6, shifter_2_p7, shifter_2_p8, shifter_2_p9, shifter_2_p10
  // shifter shifter_3: pin names not known; wires that end beside it: day23_parser_1_out_en, shifter_3_p2, C, shifter_3_p4, shifter_3_p5, shifter_3_p6, shifter_3_p7, shifter_3_p8, shifter_3_p9, shifter_3_p10
  // shifter shifter_4: pin names not known; wires that end beside it: day23_parser_1_out_en, shifter_4_p2, C, shifter_4_p4, shifter_4_p5, shifter_4_p6, shifter_4_p7, shifter_4_p8, shifter_4_p9, shifter_4_p10
  // shifter shifter_5: pin names not known; wires that end beside it: day23_parser_1_out_en, shifter_5_p2, C, shifter_5_p4, shifter_5_p5, shifter_5_p6, shifter_5_p7, shifter_5_p8, shifter_5_p9, shifter_5_p10
  // shifter shifter_6: pin names not known; wires that end beside it: day23_parser_1_out_en, shifter_6_p2, C, shifter_6_p4, shifter_6_p5, shifter_6_p6, shifter_6_p7, shifter_6_p8, shifter_6_p9, shifter_6_p10, shifter_6_p11
  Comparator #(.Bits(16)) comparator_1 (.a(counter_1_out), .b(16'h2), .eq(comparator_1_eq));  // open: gt, lt
  // Probe on shifter_1_p4
  // Probe on shifter_1_p5
  // Probe on shifter_1_p6
  // Probe on shifter_1_p7
  // Probe on shifter_1_p8
  // Probe on shifter_1_p9
  // Probe on shifter_1_p10
  // Probe on shifter_2_p2
  // Probe on shifter_2_p4
  // Probe on shifter_2_p5
  // Probe on shifter_2_p6
  // Probe on shifter_2_p7
  // Probe on shifter_2_p8
  // Probe on shifter_2_p9
  // Probe on shifter_2_p10
  // Probe on shifter_3_p2
  // Probe on shifter_3_p4
  // Probe on shifter_3_p5
  // Probe on shifter_3_p6
  // Probe on shifter_3_p7
  // Probe on shifter_3_p8
  // Probe on shifter_3_p9
  // Probe on shifter_3_p10
  // Probe on shifter_4_p2
  // Probe on shifter_4_p4
  // Probe on shifter_4_p5
  // Probe on shifter_4_p6
  // Probe on shifter_4_p7
  // Probe on shifter_4_p8
  // Probe on shifter_4_p9
  // Probe on shifter_4_p10
  // Probe on shifter_5_p2
  // Probe on shifter_5_p4
  // Probe on shifter_5_p5
  // Probe on shifter_5_p6
  // Probe on shifter_5_p7
  // Probe on shifter_5_p8
  // Probe on shifter_5_p9
  // Probe on shifter_5_p10
  // Probe on shifter_6_p2
  // Probe on shifter_6_p4
  // Probe on shifter_6_p5
  // Probe on shifter_6_p6
  // Probe on shifter_6_p7
  // Probe on shifter_6_p8
  // Probe on shifter_6_p9
  // Probe on shifter_6_p10
  // Probe on shifter_6_p11
  Break #(.Cycles(10000)) out_256 (.brk(comparator_1_eq));

  // Notes on the sheet:
  //   C: Hz: 500
endmodule
