// Digital circuit day23_node_test.dig as structural Verilog
module day23_node_test (
  input  C
);

  wire comparator_1_lt, node0_p3, node0_p5, node0_p8, node0_p9, shifter_1_p4, shifter_1_p5, shifter_1_p6,
       shifter_1_p7, shifter_1_p8, shifter_1_p9, shifter_1_p10, shifter_2_p2, shifter_2_p4, shifter_2_p5,
       shifter_2_p6, shifter_2_p7, shifter_2_p8, shifter_2_p9, shifter_2_p10, shifter_3_p2, shifter_3_p4,
       shifter_3_p5, shifter_3_p6, shifter_3_p7, shifter_3_p8, shifter_3_p9, shifter_3_p10, shifter_3_p11;
  wire [7:0] counter_1_out;
  wire [15:0] counter_2_out;
  wire [63:0] input_d;

  Counter #(.Bits(8)) counter_1 (.en(1'b1), .C(C), .clr(1'b0), .out(counter_1_out));  // open: ovf
  ROM #(.AddrBits(8), .Bits(64)) \input  (.A(counter_1_out), .sel(1'b1), .D(input_d));
  Comparator #(.Signed("true"), .Bits(64)) comparator_1 (
    .a(input_d), .b({64{1'b0}}), .lt(comparator_1_lt));  // open: gt, eq
  // Not not_1 has open pins: in=comparator_1_lt, out=open
  // day23_node #(.generic("label := \"node0\";")) node0: pin names not known; wires that end beside it: C, {64{1'b0}}, node0_p3, node0_p3, node0_p5, node0_p5, 1'b0, node0_p8, node0_p9
  LED led_1 (.in(node0_p8));
  // Probe on node0_p9
  Break break_1 (.brk(node0_p3));
  Counter #(.Bits(16)) counter_2 (.en(node0_p3), .C(C), .clr(1'b0), .out(counter_2_out));  // open: ovf
  // shifter shifter_1: pin names not known; wires that end beside it: node0_p3, node0_p5, C, shifter_1_p4, shifter_1_p5, shifter_1_p6, shifter_1_p7, shifter_1_p8, shifter_1_p9, shifter_1_p10
  // shifter shifter_2: pin names not known; wires that end beside it: node0_p3, shifter_2_p2, C, shifter_2_p4, shifter_2_p5, shifter_2_p6, shifter_2_p7, shifter_2_p8, shifter_2_p9, shifter_2_p10
  // shifter shifter_3: pin names not known; wires that end beside it: node0_p3, shifter_3_p2, C, shifter_3_p4, shifter_3_p5, shifter_3_p6, shifter_3_p7, shifter_3_p8, shifter_3_p9, shifter_3_p10, shifter_3_p11
  // Probe on counter_2_out
  // Probe on shifter_1_p4
  // Probe on shifter_1_p5
  // Probe on shifter_1_p6
  // Probe on shifter_1_p7
  // Probe on shifter_1_p8
  // Probe on shifter_1_p9
  // Probe on shifter_1_p10
  // Probe on shifter_2_p2
  // Probe on shifter_2_p4
  // Probe on shifter_2_p5
  // Probe on shifter_2_p6
  // Probe on shifter_2_p7
  // Probe on shifter_2_p8
  // Probe on shifter_2_p9
  // Probe on shifter_2_p10
  // Probe on shifter_3_p2
  // Probe on shifter_3_p4
  // Probe on shifter_3_p5
  // Probe on shifter_3_p6
  // Probe on shifter_3_p7
  // Probe on shifter_3_p8
  // Probe on shifter_3_p9
  // Probe on shifter_3_p10
  // Probe on shifter_3_p11

  // Notes on the sheet:
  //   contents of input (hex, n*v repeats v):
  //   0,47f,563a,ffffffffffffffff,ffffffffffffffff,ffffffffffffffff,ffffffffffffffff,ffffffffffffffff,
  //   ffffffffffffffff,ffffffffffffffff,ffffffffffffffff,ffffffffffffffff,ffffffffffffffff,
  //   ffffffffffffffff,ffffffffffffffff,ffffffffffffffff,ffffffffffffffff,ffffffffffffffff,
  //   ffffffffffffffff,ffffffffffffffff,ffffffffffffffff,ffffffffffffffff,ffffffffffffffff,
  //   ffffffffffffffff,ffffffffffffffff,ffffffffffffffff,ffffffffffffffff,ffffffffffffffff,
  //   ffffffffffffffff,ffffffffffffffff,ffffffffffffffff,ffffffffffffffff,ffffffffffffffff,
  //   ffffffffffffffff,ffffffffffffffff,ffffffffffffffff,ffffffffffffffff,ffffffffffffffff,
  //   ffffffffffffffff,ffffffffffffffff,ffffffffffffffff,ffffffffffffffff,ffffffffffffffff,
  //   ffffffffffffffff,ffffffffffffffff,ffffffffffffffff,ffffffffffffffff,ffffffffffffffff,
  //   ffffffffffffffff,ffffffffffffffff,ffffffffffffffff,ffffffffffffffff,ffffffffffffffff,
  //   ffffffffffffffff,ffffffffffffffff,ffffffffffffffff,ffffffffffffffff,ffffffffffffffff,
  //   ffffffffffffffff,ffffffffffffffff,ffffffffffffffff,ffffffffffffffff,ffffffffffffffff,
  //   ffffffffffffffff,ffffffffffffffff,ffffffffffffffff,ffffffffffffffff,ffffffffffffffff,
  //   ffffffffffffffff,ffffffffffffffff,ffffffffffffffff,ffffffffffffffff,ffffffffffffffff,
  //   ffffffffffffffff,ffffffffffffffff,ffffffffffffffff,ffffffffffffffff,ffffffffffffffff,
  //   ffffffffffffffff,ffffffffffffffff,ffffffffffffffff,ffffffffffffffff,ffffffffffffffff,
  //   ffffffffffffffff,ffffffffffffffff,ffffffffffffffff,ffffffffffffffff,ffffffffffffffff,
  //   ffffffffffffffff,ffffffffffffffff,ffffffffffffffff,ffffffffffffffff,ffffffffffffffff,
  //   ffffffffffffffff,ffffffffffffffff,ffffffffffffffff,ffffffffffffffff,ffffffffffffffff,
  //   ffffffffffffffff,ffffffffffffffff,ffffffffffffffff,ffffffffffffffff,ffffffffffffffff,
  //   ffffffffffffffff,ffffffffffffffff,ffffffffffffffff,ffffffffffffffff,ffffffffffffffff,
  //   ffffffffffffffff,ffffffffffffffff,ffffffffffffffff,ffffffffffffffff,ffffffffffffffff,
  //   ffffffffffffffff,ffffffffffffffff,ffffffffffffffff,ffffffffffffffff,ffffffffffffffff,
  //   ffffffffffffffff,ffffffffffffffff,ffffffffffffffff,ffffffffffffffff,ffffffffffffffff,
  //   ffffffffffffffff,ffffffffffffffff,ffffffffffffffff,ffffffffffffffff,ffffffffffffffff,
  //   ffffffffffffffff,ffffffffffffffff,ffffffffffffffff,ffffffffffffffff,ffffffffffffffff,
  //   ffffffffffffffff,ffffffffffffffff,ffffffffffffffff,ffffffffffffffff,ffffffffffffffff,
  //   ffffffffffffffff,ffffffffffffffff,ffffffffffffffff,ffffffffffffffff,ffffffffffffffff,
  //   ffffffffffffffff,ffffffffffffffff,ffffffffffffffff,ffffffffffffffff,ffffffffffffffff,
  //   ffffffffffffffff,ffffffffffffffff,ffffffffffffffff,ffffffffffffffff,ffffffffffffffff,
  //   ffffffffffffffff,ffffffffffffffff,ffffffffffffffff,ffffffffffffffff,ffffffffffffffff,
  //   ffffffffffffffff,ffffffffffffffff,ffffffffffffffff,ffffffffffffffff,ffffffffffffffff,
  //   ffffffffffffffff,ffffffffffffffff,ffffffffffffffff,ffffffffffffffff,ffffffffffffffff,
  //   ffffffffffffffff,ffffffffffffffff,ffffffffffffffff,ffffffffffffffff,ffffffffffffffff,
  //   ffffffffffffffff,ffffffffffffffff,ffffffffffffffff,ffffffffffffffff,ffffffffffffffff,
  //   ffffffffffffffff,ffffffffffffffff,ffffffffffffffff,ffffffffffffffff,ffffffffffffffff,
  //   ffffffffffffffff,ffffffffffffffff,ffffffffffffffff,ffffffffffffffff,ffffffffffffffff,
  //   ffffffffffffffff,ffffffffffffffff,ffffffffffffffff,ffffffffffffffff,ffffffffffffffff,
  //   ffffffffffffffff,ffffffffffffffff,ffffffffffffffff,ffffffffffffffff,ffffffffffffffff,
  //   ffffffffffffffff,ffffffffffffffff,ffffffffffffffff,ffffffffffffffff,ffffffffffffffff,
  //   ffffffffffffffff,ffffffffffffffff,ffffffffffffffff,ffffffffffffffff,ffffffffffffffff,
  //   ffffffffffffffff,ffffffffffffffff,ffffffffffffffff,ffffffffffffffff,ffffffffffffffff,
  //   ffffffffffffffff,ffffffffffffffff,ffffffffffffffff,ffffffffffffffff,ffffffffffffffff,
  //   ffffffffffffffff,ffffffffffffffff,ffffffffffffffff,ffffffffffffffff,ffffffffffffffff,
  //   ffffffffffffffff,ffffffffffffffff,ffffffffffffffff,ffffffffffffffff,ffffffffffffffff,
  //   ffffffffffffffff,ffffffffffffffff,ffffffffffffffff,ffffffffffffffff,ffffffffffffffff,
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endmodule
