// Digital circuit fifo.dig as structural Verilog
module fifo (
  input  C,
  input  in_en,
  input  [63:0] in_val,
  input  out_en,
  output out_avail,
  output [63:0] out_val,
  output [7:0] cnt
);

  wire [7:0] out_cnt_out;

  Counter #(.Bits(8)) in_cnt (.en(in_en), .C(C), .clr(1'b0), .out(cnt));  // open: ovf
  Counter #(.Bits(8)) out_cnt (.en(out_en), .C(C), .clr(1'b0), .out(out_cnt_out));  // open: ovf
  RAMDualAccess #(.AddrBits(8), .Bits(64)) ramdualaccess_1 (
    .str(in_en), .C(C), .ld(1'b1), .A1(cnt), .Din1(in_val), .A2(out_cnt_out), .D2(out_val));  // open: D1
  Comparator #(.Bits(8)) comparator_1 (.a(out_cnt_out), .b(cnt), .lt(out_avail));  // open: gt, eq
endmodule
